// Logisim project DESIGN_CPU.circ as structural Verilog: 5 circuits, main circuit main
module main (
  input  [7:0] in_1,
  input  in_2,
  input  in_3,
  output [7:0] out_4
);

  CPU_REG_8 cpu_reg_8_1 (.in_1(in_1), .out_4(out_4), .in_2(in_3), .in_3(in_2));
endmodule

module CPU_MEM_8 (
  input  [7:0] i,
  input  s,
  output [7:0] o
);

  CPU_MEM_1 cpu_mem_1_1 (.s(i[0]), .e_2(o[0]), .e(s));
  CPU_MEM_1 cpu_mem_1_2 (.s(i[1]), .e_2(o[1]), .e(s));
  CPU_MEM_1 cpu_mem_1_3 (.s(i[2]), .e_2(o[2]), .e(s));
  CPU_MEM_1 cpu_mem_1_4 (.s(i[3]), .e_2(o[3]), .e(s));
  CPU_MEM_1 cpu_mem_1_5 (.s(i[4]), .e_2(o[4]), .e(s));
  CPU_MEM_1 cpu_mem_1_6 (.s(i[5]), .e_2(o[5]), .e(s));
  CPU_MEM_1 cpu_mem_1_7 (.s(i[6]), .e_2(o[6]), .e(s));
  CPU_MEM_1 cpu_mem_1_8 (.s(i[7]), .e_2(o[7]), .e(s));
endmodule

module CPU_ENABLE (
  input  [7:0] in_1,
  input  in_2,
  output [7:0] out_3
);

  and and_1 (out_3[0], in_1[0], in_2);
  and and_2 (out_3[1], in_1[1], in_2);
  and and_3 (out_3[2], in_1[2], in_2);
  and and_4 (out_3[3], in_1[3], in_2);
  and and_5 (out_3[4], in_1[4], in_2);
  and and_6 (out_3[5], in_1[5], in_2);
  and and_7 (out_3[6], in_1[6], in_2);
  and and_8 (out_3[7], in_1[7], in_2);
endmodule

module CPU_REG_8 (
  input  [7:0] in_1,
  input  in_2,
  input  in_3,
  output [7:0] out_4
);

  wire [7:0] cpu_mem_8_1_o;

  CPU_MEM_8 cpu_mem_8_1 (.i(in_1), .s(in_2), .o(cpu_mem_8_1_o));
  CPU_ENABLE cpu_enable_1 (.out_3(out_4), .in_1(cpu_mem_8_1_o), .in_2(in_3));
endmodule

module CPU_DECODE_2X4 (
  input  in_1,
  input  in_2,
  output out_3,
  output out_4,
  output out_5,
  output out_6
);

  wire not_1_out, not_2_out;

  not not_1 (not_1_out, in_1);
  not not_2 (not_2_out, in_2);
  and and_1 (out_3, not_1_out, not_2_out);
  and and_2 (out_4, not_1_out, in_2);
  and and_3 (out_5, in_1, not_2_out);
  and and_4 (out_6, in_1, in_2);
endmodule
